// Logisim project ZCS.circ as structural Verilog: 23 circuits, main circuit main
module main (
);

  wire button_1_out, clock_1_out, clock_2_out;

  Clock #(.highDuration(2), .lowDuration(2)) clock_1 (.out(clock_1_out));
  Clock #(.highDuration(2), .lowDuration(2), .phaseOffset(1)) clock_2 (.out(clock_2_out));
  Button button_1 (.out(button_1_out));
endmodule

module alu (
  input  Carry_In,
  input  Carry_Usage,
  input  OE,
  input  [7:0] Accumulator,
  input  [7:0] Temp,
  input  [5:0] Operation,
  output SF,
  output [7:0] ALU_Out,
  output Carry_Out
);

  wire and_1_out, or_2_out, xor_1_out;
  wire [7:0] adder_1_out, and_2_out, busbuffercntrl_1_a_out, not_1_out, or_1_out, xor_2_out, xor_3_out;

  and and_1 (and_1_out, Carry_Usage, Carry_In);
  xor xor_1 (xor_1_out, and_1_out, Operation[1]);
  assign xor_2_out = Temp ^ {8{Operation[1]}};  // XOR_Gate xor_2, 8 bits wide
  BusBufferCntrl busbuffercntrl_1 (.A_Out(busbuffercntrl_1_a_out), .A_In(and_2_out), .Control(Operation[2]));
  assign and_2_out = Accumulator & Temp;  // AND_Gate and_2, 8 bits wide
  BusBufferCntrl busbuffercntrl_2 (.A_Out(busbuffercntrl_1_a_out), .A_In(or_1_out), .Control(Operation[3]));
  assign or_1_out = Accumulator | Temp;  // OR_Gate or_1, 8 bits wide
  BusBufferCntrl busbuffercntrl_3 (.A_Out(busbuffercntrl_1_a_out), .A_In(xor_3_out), .Control(Operation[4]));
  assign xor_3_out = Accumulator ^ Temp;  // XOR_Gate xor_3, 8 bits wide
  BusBufferCntrl busbuffercntrl_4 (.A_Out(busbuffercntrl_1_a_out), .A_In(not_1_out), .Control(Operation[5]));
  assign not_1_out = ~Accumulator;  // NOT_Gate not_1, 8 bits wide
  or or_2 (or_2_out, Operation[1], Operation[0]);
  BusBufferCntrl busbuffercntrl_5 (.A_Out(busbuffercntrl_1_a_out), .A_In(adder_1_out), .Control(or_2_out));
  Adder adder_1 (.a(Accumulator), .b(xor_2_out), .out(adder_1_out), .cin(xor_1_out), .cout(Carry_Out));
  BusBufferCntrl busbuffercntrl_6 (.A_Out(ALU_Out), .A_In(busbuffercntrl_1_a_out), .Control(OE));

  assign SF = OE;
endmodule

module prom (
  input  [12:0] AddressBus,
  input  MEMR,
  output [7:0] DataBus
);

  wire [7:0] rom_1_data;

  ROM #(.addrWidth(13)) rom_1 (.addr(AddressBus), .data(rom_1_data));
  and and_1 (DataBus[0], rom_1_data[0], MEMR);
  and and_2 (DataBus[1], rom_1_data[1], MEMR);
  and and_3 (DataBus[2], rom_1_data[2], MEMR);
  and and_4 (DataBus[3], rom_1_data[3], MEMR);
  and and_5 (DataBus[4], rom_1_data[4], MEMR);
  and and_6 (DataBus[5], rom_1_data[5], MEMR);
  and and_7 (DataBus[6], rom_1_data[6], MEMR);
  and and_8 (DataBus[7], rom_1_data[7], MEMR);
endmodule

module ram_mem (
  input  [12:0] AddressBus,
  input  WE,
  input  OE,
  input  CLK,
  output [7:0] DataBus
);

  RAM #(.addrWidth(13), .databus("bidir")) ram_1 (.addr(AddressBus), .we(WE), .oe(OE), .clk(CLK), .data(DataBus));
endmodule

module cpu (
);

  wire addrdec_1_key_ctrl, addrdec_1_key_data, addrdec_1_ram_r, addrdec_1_ram_w, addrdec_1_rom_e,
       addrdec_1_scr_data, addrdec_1_x_pos, addrdec_1_y_pos, ALU_OE, ALUnit_carry_out, ALUnit_sf, and_1_out,
       and_2_out, AOE, AWE, clock_1_out, control_1_mem_r, control_1_mem_w, control_1_r_mux_ctrl,
       FlagsFlipFlop_carry_out, HL_OE, INC_DEC, instructiondecoder_1_aluop, instructiondecoder_1_carryusage,
       instructiondecoder_1_cmp, instructiondecoder_1_hlt, instructiondecoder_1_jr, instructiondecoder_1_js,
       instructiondecoder_1_lpc, instructiondecoder_1_lsp, instructiondecoder_1_mir,
       instructiondecoder_1_mov, instructiondecoder_1_mvmem, instructiondecoder_1_push,
       instructiondecoder_1_spop, instructiondecoder_1_tomem, IR_WE, j_k_ff_1_q, j_k_ff_2_q, not_1_out,
       PC_WE, R_OE, R_WE, RST, SP_PC, SP_WE, TMP_OE, TMP_WE;
  wire [1:0] control_1_addr_mux, count_1_cnt, FlagMux;
  wire [2:0] REGMUX, REGMUX_I;
  wire [3:0] FL;
  wire [5:0] instructiondecoder_1_add;
  wire [6:0] keyboard_1_data;
  wire [7:0] Accumulator_d_out, Accumulator_dout, instrreg_1_d_out, register_1_q, register_2_q, register_5_q,
       rom_1_data, Temp_d_out;
  wire [7:7] keyboard_1_avail;
  wire [14:0] addrdec_1_addr;
  wire [15:0] reg_mult_1_addrbus;

  J_K_Flip_Flop #(.trigger("falling")) j_k_ff_1 (
    .J(1'b1), .K(1'b1), .clk(clock_1_out), .Q(j_k_ff_1_q));  // open: Qn, preset, reset
  Clock clock_1 (.out(clock_1_out));
  J_K_Flip_Flop j_k_ff_2 (.J(1'b1), .K(1'b1), .clk(clock_1_out), .Q(j_k_ff_2_q));  // open: Qn, preset, reset
  regs Accumulator (
    .DOUT(Accumulator_dout), .D_Out(Accumulator_d_out), .OE(AOE), .WE(AWE), .R(RST), .CLK(and_1_out),
    .DIN(Accumulator_dout));
  Counter #(.max('hffff), .width(16)) counter_1 (
    .clr(RST), .load(1'b0), .up(1'b1), .count(1'b1), .clk(count_1_cnt[1]));  // open: D, carry, Q
  regs Temp (
    .DOUT(Accumulator_dout), .D_Out(Temp_d_out), .OE(TMP_OE), .WE(TMP_WE), .R(RST), .CLK(and_1_out),
    .DIN(Accumulator_dout));
  not not_1 (not_1_out, instructiondecoder_1_hlt);
  and and_1 (and_1_out, not_1_out, j_k_ff_1_q);
  and and_2 (and_2_out, not_1_out, j_k_ff_2_q);
  Button button_1 (.out(RST));
  count count_1 (.CNT(count_1_cnt), .CLK(and_2_out), .RST(RST));
  LED led_1 (.in(count_1_cnt[1]));
  LED led_2 (.in(count_1_cnt[0]));
  flags FlagsFlipFlop (
    .DOUT(FL), .Carry_Out(FlagsFlipFlop_carry_out), .Carry_In(ALUnit_carry_out), .WE(ALUnit_sf),
    .CLK(and_1_out), .R(RST), .DIN(Accumulator_dout));
  alu ALUnit (
    .SF(ALUnit_sf), .ALU_Out(Accumulator_dout), .Carry_Out(ALUnit_carry_out),
    .Operation(instructiondecoder_1_add), .OE(ALU_OE), .Accumulator(Accumulator_d_out), .Temp(Temp_d_out),
    .Carry_Usage(instructiondecoder_1_carryusage), .Carry_In(FlagsFlipFlop_carry_out));
  InstrReg instrreg_1 (.D_Out(instrreg_1_d_out), .WE(IR_WE), .R(RST), .CLK(and_1_out), .DIN(Accumulator_dout));
  InstructionDecoder instructiondecoder_1 (
    .CarryUsage(instructiondecoder_1_carryusage), .Add(instructiondecoder_1_add[0]),
    .Sub(instructiondecoder_1_add[1]), .CMP(instructiondecoder_1_cmp), .ANDr(instructiondecoder_1_add[2]),
    .ORr(instructiondecoder_1_add[3]), .XRr(instructiondecoder_1_add[4]), .NTr(instructiondecoder_1_add[5]),
    .SPOP(instructiondecoder_1_spop), .ALUOP(instructiondecoder_1_aluop), .RegMux(REGMUX_I),
    .LPC(instructiondecoder_1_lpc), .JS(instructiondecoder_1_js), .JR(instructiondecoder_1_jr),
    .FLAGMUX(FlagMux), .LSP(instructiondecoder_1_lsp), .HLT(instructiondecoder_1_hlt),
    .MIr(instructiondecoder_1_mir), .MOV(instructiondecoder_1_mov), .ToMem(instructiondecoder_1_tomem),
    .MVMEM(instructiondecoder_1_mvmem), .PUSH(instructiondecoder_1_push), .InstructionReg(instrreg_1_d_out),
    .RMuxCtrl(control_1_r_mux_ctrl));
  control control_1 (
    .SP_WE(SP_WE), .ALU_OE(ALU_OE), .REGMUX_O(REGMUX), .PC_WE(PC_WE), .SP_PC(SP_PC),
    .ADDR_MUX(control_1_addr_mux), .IR_WE(IR_WE), .R_MUX_CTRL(control_1_r_mux_ctrl), .R_WE(R_WE),
    .TMP_OE(TMP_OE), .TMP_WE(TMP_WE), .R_OE(R_OE), .MEM_W(control_1_mem_w), .HL_OE(HL_OE),
    .MEM_R(control_1_mem_r), .INC_DEC(INC_DEC), .CMP(instructiondecoder_1_cmp), .FMUX(FlagMux), .FLAGS(FL),
    .C2(and_2_out), .EXC(count_1_cnt), .REGMUX_I(REGMUX_I), .MIV(instructiondecoder_1_mir),
    .LSP(instructiondecoder_1_lsp), .LPC(instructiondecoder_1_lpc), .JS(instructiondecoder_1_js),
    .JR(instructiondecoder_1_jr), .ALUOP(instructiondecoder_1_aluop), .MOV(instructiondecoder_1_mov),
    .MEM_MOV(instructiondecoder_1_mvmem), .MEM_DIR(instructiondecoder_1_tomem),
    .SP_OP(instructiondecoder_1_spop), .PUSH(instructiondecoder_1_push));
  addrdec addrdec_1 (
    .SCR_DATA(addrdec_1_scr_data), .addr(addrdec_1_addr), .KEY_CTRL(addrdec_1_key_ctrl),
    .KEY_DATA(addrdec_1_key_data), .X_POS(addrdec_1_x_pos), .Y_POS(addrdec_1_y_pos), .ROM_E(addrdec_1_rom_e),
    .RAM_R(addrdec_1_ram_r), .RAM_W(addrdec_1_ram_w), .MR(control_1_mem_r), .MW(control_1_mem_w),
    .Address(reg_mult_1_addrbus));
  reg_mult reg_mult_1 (
    .DOUT(Accumulator_dout), .A_WE(AWE), .AddrBus(reg_mult_1_addrbus), .A_OE(AOE), .INC_DEC(INC_DEC),
    .CLK(and_1_out), .OE(R_OE), .WE(R_WE), .Reset(RST), .PC_WE(PC_WE), .DIN(Accumulator_dout), .HL_OE(HL_OE),
    .AddrMul(control_1_addr_mux), .DataMUL(REGMUX), .SP_WE(SP_WE), .SP_PC(SP_PC));
  ROM #(.addrWidth(15)) rom_1 (.addr(addrdec_1_addr), .data(rom_1_data));
  RAM #(.addrWidth(15), .databus("bidir"), .trigger("high")) ram_1 (
    .addr(addrdec_1_addr), .we(addrdec_1_ram_w), .oe(addrdec_1_ram_r), .data(Accumulator_dout));
  BusBufferCntrl busbuffercntrl_1 (.A_Out(Accumulator_dout), .A_In(rom_1_data), .Control(addrdec_1_rom_e));
  Register #(.trigger("high")) register_1 (
    .D(Accumulator_dout), .en(addrdec_1_key_ctrl), .clk(1'b1), .Q(register_1_q), .clr(RST));
  Register #(.trigger("high")) register_2 (
    .D(Accumulator_dout), .en(addrdec_1_x_pos), .clk(1'b1), .Q(register_2_q), .clr(RST));
  Register #(.trigger("high")) register_3 (
    .D(Accumulator_dout), .en(addrdec_1_y_pos), .clk(1'b1), .Q(register_2_q), .clr(RST));
  Register #(.trigger("high")) register_4 (
    .D(Accumulator_dout), .en(addrdec_1_scr_data), .clk(1'b1), .Q(register_2_q));  // open: clr
  Keyboard keyboard_1 (
    .clk(register_1_q[0]), .re(register_1_q[1]), .clr(register_1_q[2]), .avail(keyboard_1_avail[7]),
    .data(keyboard_1_data));
  Register #(.trigger("high")) register_5 (
    .D({keyboard_1_avail[7], keyboard_1_data}), .en(1'b1), .clk(1'b1), .Q(register_5_q), .clr(RST));
  BusBufferCntrl busbuffercntrl_2 (.A_Out(Accumulator_dout), .A_In(register_5_q), .Control(addrdec_1_key_data));

  // Notes on the sheet:
  //   contents of rom_1 (hex, n*v repeats v):
  //   0 3 1 1 8a ff 0 6 10 37 2f 5 0 6 4f 24 ff 45 4e 0 1 b0 46 2f 37 5 0 6 26 c4 3e 3d 0 1 a8 45 2f 37 39
  //   38 3d 3e 24 f 17 1f 5 f0 6 1 78 7 1 80 c8 8c 38 5 0 6 2e c4 ca 5 f0 6 0 2 3 3 2 57 5f 3b 3a 39 3d 3e
  //   24 f 17 2 0 5 0 6 5e 37 2f 5 0 6 2b 24 1 a 8c 5 0 6 73 cc 5 83 56 47 0 1 90 42 5 0 6 53 24 5 83 56 0
  //   0 47 50 3a 39 3d 3e 24
endmodule

module regs (
  input  OE,
  input  WE,
  input  R,
  input  [7:0] DIN,
  input  CLK,
  output [7:0] DOUT,
  output [7:0] D_Out
);

  Register register_1 (.D(DIN), .en(WE), .clk(CLK), .Q(D_Out), .clr(R));
  BusBufferCntrl busbuffercntrl_1 (.A_Out(DOUT), .A_In(D_Out), .Control(OE));
endmodule

module BusTrans (
  input  DIR_N,
  input  OE_N,
  input  [7:0] A,
  input  [7:0] B
);

  wire and_1_out, and_2_out;

  and and_1 (and_1_out, DIR_N, ~OE_N);  // AND_Gate
  assign B[0] = and_1_out ? A[0] : 1'bz;  // Controlled_Buffer controlled_buffer_1
  assign B[1] = and_1_out ? A[1] : 1'bz;  // Controlled_Buffer controlled_buffer_2
  assign B[2] = and_1_out ? A[2] : 1'bz;  // Controlled_Buffer controlled_buffer_3
  assign B[3] = and_1_out ? A[3] : 1'bz;  // Controlled_Buffer controlled_buffer_4
  assign B[4] = and_1_out ? A[4] : 1'bz;  // Controlled_Buffer controlled_buffer_5
  assign B[5] = and_1_out ? A[5] : 1'bz;  // Controlled_Buffer controlled_buffer_6
  assign B[6] = and_1_out ? A[6] : 1'bz;  // Controlled_Buffer controlled_buffer_7
  assign B[7] = and_1_out ? A[7] : 1'bz;  // Controlled_Buffer controlled_buffer_8
  and and_2 (and_2_out, ~DIR_N, ~OE_N);  // AND_Gate
  assign A[0] = and_2_out ? B[0] : 1'bz;  // Controlled_Buffer controlled_buffer_9
  assign A[1] = and_2_out ? B[1] : 1'bz;  // Controlled_Buffer controlled_buffer_10
  assign A[2] = and_2_out ? B[2] : 1'bz;  // Controlled_Buffer controlled_buffer_11
  assign A[3] = and_2_out ? B[3] : 1'bz;  // Controlled_Buffer controlled_buffer_12
  assign A[4] = and_2_out ? B[4] : 1'bz;  // Controlled_Buffer controlled_buffer_13
  assign A[5] = and_2_out ? B[5] : 1'bz;  // Controlled_Buffer controlled_buffer_14
  assign A[6] = and_2_out ? B[6] : 1'bz;  // Controlled_Buffer controlled_buffer_15
  assign A[7] = and_2_out ? B[7] : 1'bz;  // Controlled_Buffer controlled_buffer_16
endmodule

module LogicGate (
  input  Control,
  input  [7:0] B_In,
  input  [7:0] A_In,
  output [7:0] A_Out,
  output [7:0] B_Out
);

  and and_1 (A_Out[0], A_In[0], Control);
  and and_2 (B_Out[0], B_In[0], Control);
  and and_3 (A_Out[1], A_In[1], Control);
  and and_4 (B_Out[1], B_In[1], Control);
  and and_5 (A_Out[2], A_In[2], Control);
  and and_6 (B_Out[2], B_In[2], Control);
  and and_7 (A_Out[3], A_In[3], Control);
  and and_8 (B_Out[3], B_In[3], Control);
  and and_9 (A_Out[4], A_In[4], Control);
  and and_10 (B_Out[4], B_In[4], Control);
  and and_11 (A_Out[5], A_In[5], Control);
  and and_12 (B_Out[5], B_In[5], Control);
  and and_13 (A_Out[6], A_In[6], Control);
  and and_14 (B_Out[6], B_In[6], Control);
  and and_15 (A_Out[7], A_In[7], Control);
  and and_16 (B_Out[7], B_In[7], Control);
endmodule

module Bus2BufferCntrl (
  input  Control,
  input  [7:0] B_In,
  input  [7:0] A_In,
  output [7:0] A_Out,
  output [7:0] B_Out
);

  and and_1 (A_Out[0], A_In[0], Control);
  and and_2 (B_Out[0], B_In[0], Control);
  and and_3 (A_Out[1], A_In[1], Control);
  and and_4 (B_Out[1], B_In[1], Control);
  and and_5 (A_Out[2], A_In[2], Control);
  and and_6 (B_Out[2], B_In[2], Control);
  and and_7 (A_Out[3], A_In[3], Control);
  and and_8 (B_Out[3], B_In[3], Control);
  and and_9 (A_Out[4], A_In[4], Control);
  and and_10 (B_Out[4], B_In[4], Control);
  and and_11 (A_Out[5], A_In[5], Control);
  and and_12 (B_Out[5], B_In[5], Control);
  and and_13 (A_Out[6], A_In[6], Control);
  and and_14 (B_Out[6], B_In[6], Control);
  and and_15 (A_Out[7], A_In[7], Control);
  and and_16 (B_Out[7], B_In[7], Control);
endmodule

module BusBufferCntrl (
  input  Control,
  input  [7:0] A_In,
  output [7:0] A_Out
);

  assign A_Out[0] = Control ? A_In[0] : 1'bz;  // Controlled_Buffer controlled_buffer_1
  assign A_Out[1] = Control ? A_In[1] : 1'bz;  // Controlled_Buffer controlled_buffer_2
  assign A_Out[2] = Control ? A_In[2] : 1'bz;  // Controlled_Buffer controlled_buffer_3
  assign A_Out[3] = Control ? A_In[3] : 1'bz;  // Controlled_Buffer controlled_buffer_4
  assign A_Out[4] = Control ? A_In[4] : 1'bz;  // Controlled_Buffer controlled_buffer_5
  assign A_Out[5] = Control ? A_In[5] : 1'bz;  // Controlled_Buffer controlled_buffer_6
  assign A_Out[6] = Control ? A_In[6] : 1'bz;  // Controlled_Buffer controlled_buffer_7
  assign A_Out[7] = Control ? A_In[7] : 1'bz;  // Controlled_Buffer controlled_buffer_8
endmodule

module flags (
  input  Carry_In,
  input  WE,
  input  CLK,
  input  R,
  input  [7:0] DIN,
  output [3:0] DOUT,
  output Carry_Out
);

  wire [3:3] and_1_out;

  and and_1 (and_1_out[3], ~DIN[0], ~DIN[1], ~DIN[2], ~DIN[3], ~DIN[4], ~DIN[5], ~DIN[6], ~DIN[7]);  // AND_Gate
  Register #(.width(4)) register_1 (
    .D({and_1_out[3], DIN[7], DIN[0], Carry_In}), .en(WE), .clk(CLK), .Q({DOUT[3:1], Carry_Out}), .clr(R));

  assign DOUT[0] = Carry_Out;
endmodule

module InstructionDecoder (
  input  [7:0] InstructionReg,
  input  RMuxCtrl,
  output [2:0] RegMux,
  output HLT,
  output MIr,
  output LSP,
  output MOV,
  output ToMem,
  output MVMEM,
  output ALUOP,
  output CarryUsage,
  output Add,
  output Sub,
  output CMP,
  output ANDr,
  output ORr,
  output XRr,
  output NTr,
  output LPC,
  output JS,
  output JR,
  output [1:0] FLAGMUX,
  output PUSH,
  output SPOP
);

  wire and_2_out, and_6_out, and_7_out, and_8_out, and_12_out, and_13_out, and_14_out, demultiplexer_1_out0,
       demultiplexer_1_out1, demultiplexer_1_out2, demultiplexer_1_out3, demultiplexer_1_out6, nand_1_out,
       xor_1_out;
  wire [2:0] and_17_out, and_18_out, and_20_out, and_21_out, and_22_out, and_23_out, and_24_out, and_25_out,
       and_26_out, and_27_out, not_1_out, not_2_out;
  wire [2:2] or_1_out;

  and and_1 (HLT, InstructionReg[0], InstructionReg[1], InstructionReg[2], InstructionReg[3], InstructionReg[4], InstructionReg[5], InstructionReg[6], InstructionReg[7]);
  nand nand_1 (nand_1_out, InstructionReg[0], InstructionReg[1], InstructionReg[2]);
  and and_2 (and_2_out, ~InstructionReg[3], ~InstructionReg[4], ~InstructionReg[5], ~InstructionReg[6], ~InstructionReg[7]);  // AND_Gate
  and and_3 (LSP, InstructionReg[0], InstructionReg[1], InstructionReg[2], InstructionReg[3], InstructionReg[4], InstructionReg[5], ~InstructionReg[6], ~InstructionReg[7]);  // AND_Gate
  and and_4 (MOV, InstructionReg[6], ~InstructionReg[7]);  // AND_Gate
  and and_5 (ToMem, InstructionReg[0], InstructionReg[1], InstructionReg[2]);
  and and_6 (and_6_out, InstructionReg[3], InstructionReg[4], InstructionReg[5]);
  and and_7 (and_7_out, ~InstructionReg[6], InstructionReg[7]);  // AND_Gate
  and and_8 (and_8_out, ~InstructionReg[2], InstructionReg[7], InstructionReg[6], ~HLT);  // AND_Gate
  and and_9 (LPC, ~InstructionReg[0], ~InstructionReg[1], InstructionReg[2], ~InstructionReg[3], ~InstructionReg[4], InstructionReg[5], ~InstructionReg[6], ~InstructionReg[7]);  // AND_Gate
  and and_10 (JS, ~InstructionReg[0], ~InstructionReg[1], InstructionReg[2], InstructionReg[3], InstructionReg[6], InstructionReg[7]);  // AND_Gate
  and and_11 (JR, ~InstructionReg[0], ~InstructionReg[1], InstructionReg[2], ~InstructionReg[3], InstructionReg[6], InstructionReg[7]);  // AND_Gate
  and and_12 (and_12_out, InstructionReg[0], InstructionReg[1], InstructionReg[2]);
  and and_13 (and_13_out, InstructionReg[3], InstructionReg[4], InstructionReg[5]);
  and and_14 (and_14_out, ~InstructionReg[6], ~InstructionReg[7]);  // AND_Gate
  and and_15 (MIr, nand_1_out, and_2_out);
  or or_1 (or_1_out[2], and_7_out, and_8_out);
  and and_16 (PUSH, and_12_out, ~and_13_out);  // AND_Gate
  assign and_17_out = InstructionReg[2:0] & {3{MIr}};  // AND_Gate and_17, 3 bits wide
  or or_2 (MVMEM, ToMem, and_6_out);
  assign not_1_out = ~{3{RMuxCtrl}};  // NOT_Gate not_1, 3 bits wide
  assign and_18_out = {3{or_1_out[2]}} & InstructionReg[5:3];  // AND_Gate and_18, 3 bits wide
  and and_19 (CarryUsage, ~InstructionReg[2], and_7_out, InstructionReg[0]);  // AND_Gate
  assign not_2_out = ~{3{PUSH}};  // NOT_Gate not_2, 3 bits wide
  assign and_20_out = {3{MOV}} & and_21_out;  // AND_Gate and_20, 3 bits wide
  assign and_21_out = InstructionReg[2:0] & {3{RMuxCtrl}};  // AND_Gate and_21, 3 bits wide
  assign and_22_out = {3{MOV}} & and_23_out;  // AND_Gate and_22, 3 bits wide
  assign and_23_out = not_1_out & InstructionReg[5:3];  // AND_Gate and_23, 3 bits wide
  Demultiplexer #(.select(3)) demultiplexer_1 (
    .out0(demultiplexer_1_out0), .out1(demultiplexer_1_out1), .out2(demultiplexer_1_out2),
    .out3(demultiplexer_1_out3), .out4(CMP), .out6(demultiplexer_1_out6), .out7(demultiplexer_1_out6),
    .in(and_7_out), .sel(InstructionReg[2:0]));  // open: out5
  Demultiplexer #(.select(3)) demultiplexer_2 (
    .out0(ANDr), .out1(ORr), .out2(XRr), .out3(NTr), .in(and_8_out), .sel(InstructionReg[2:0]));  // open: out4, out5, out6, out7
  xor xor_1 (xor_1_out, and_12_out, and_13_out);
  assign and_24_out = {3{SPOP}} & and_25_out;  // AND_Gate and_24, 3 bits wide
  assign and_25_out = InstructionReg[2:0] & not_2_out;  // AND_Gate and_25, 3 bits wide
  assign and_26_out = {3{SPOP}} & and_27_out;  // AND_Gate and_26, 3 bits wide
  assign and_27_out = {3{PUSH}} & InstructionReg[5:3];  // AND_Gate and_27, 3 bits wide
  or or_3 (Add, demultiplexer_1_out0, demultiplexer_1_out1);
  or or_4 (Sub, demultiplexer_1_out2, CMP, demultiplexer_1_out3);
  and and_28 (SPOP, xor_1_out, and_14_out);
  or or_5 (ALUOP, and_7_out, and_8_out);
  assign RegMux = and_17_out | and_20_out | and_22_out | and_18_out | and_24_out | and_26_out;  // OR_Gate or_6, 3 bits wide

  assign FLAGMUX = InstructionReg[5:4];
endmodule

module reg_mult (
  input  [7:0] DIN,
  input  [2:0] DataMUL,
  input  A_OE,
  input  WE,
  input  OE,
  input  CLK,
  input  Reset,
  input  SP_WE,
  input  HL_OE,
  input  PC_WE,
  input  SP_PC,
  input  INC_DEC,
  input  [1:0] AddrMul,
  output [7:0] DOUT,
  output A_WE,
  output [15:0] AddrBus
);

  wire demultiplexer_1_out1, demultiplexer_1_out2, demultiplexer_1_out3, demultiplexer_1_out4,
       demultiplexer_1_out5, demultiplexer_1_out6, demultiplexer_2_out1, demultiplexer_2_out2,
       demultiplexer_2_out3, demultiplexer_2_out4, demultiplexer_2_out5, demultiplexer_2_out6, not_1_out,
       or_1_out;
  wire [7:0] B_dout;
  wire [15:0] adder_1_out, controlled_buffer_1_out, hl_1_d_out, multiplexer_2_out, multiplexer_3_out,
       pc_1_d_out, stack_pointer_1_d_out;

  Demultiplexer #(.enable("true"), .select(3)) demultiplexer_1 (
    .out0(A_WE), .out1(demultiplexer_1_out1), .out2(demultiplexer_1_out2), .out3(demultiplexer_1_out3),
    .out4(demultiplexer_1_out4), .out5(demultiplexer_1_out5), .out6(demultiplexer_1_out6), .in(WE),
    .sel(DataMUL), .en(WE));  // open: out7
  regs B (
    .DOUT(B_dout), .OE(demultiplexer_2_out1), .WE(demultiplexer_1_out1), .R(Reset), .CLK(CLK), .DIN(DIN));  // open: D_Out
  regs D (
    .DOUT(B_dout), .OE(demultiplexer_2_out3), .WE(demultiplexer_1_out3), .R(Reset), .CLK(CLK), .DIN(DIN));  // open: D_Out
  HL hl_1 (
    .DOUT_H(B_dout), .DOUT_L(B_dout), .D_Out(hl_1_d_out), .OE_L(demultiplexer_2_out6),
    .OE_H(demultiplexer_2_out5), .R(Reset), .WE_H(demultiplexer_1_out5), .WE_L(demultiplexer_1_out6),
    .CLK(CLK), .DIN_H(DIN), .DIN_L(DIN));
  assign controlled_buffer_1_out = HL_OE ? hl_1_d_out : 16'bz;  // Controlled_Buffer controlled_buffer_1
  PC pc_1 (.D_Out(pc_1_d_out), .WE(PC_WE), .R(Reset), .CLK(CLK), .DIN(controlled_buffer_1_out));
  Multiplexer #(.select(2), .width(16)) multiplexer_1 (
    .in0(pc_1_d_out), .in1(stack_pointer_1_d_out), .in2(controlled_buffer_1_out), .out(AddrBus), .sel(AddrMul));  // open: in3
  regs C (
    .DOUT(B_dout), .OE(demultiplexer_2_out2), .WE(demultiplexer_1_out2), .R(Reset), .CLK(CLK), .DIN(DIN));  // open: D_Out
  regs regs_1 (
    .DOUT(B_dout), .OE(demultiplexer_2_out4), .WE(demultiplexer_1_out4), .R(Reset), .CLK(CLK), .DIN(DIN));  // open: D_Out
  not not_1 (not_1_out, HL_OE);
  assign controlled_buffer_1_out = not_1_out ? adder_1_out : 16'bz;  // Controlled_Buffer controlled_buffer_2
  stack_pointer stack_pointer_1 (
    .D_Out(stack_pointer_1_d_out), .R(Reset), .WE(SP_WE), .CLK(CLK), .DIN(controlled_buffer_1_out));
  Multiplexer #(.width(16)) multiplexer_2 (
    .in0(stack_pointer_1_d_out), .in1(pc_1_d_out), .out(multiplexer_2_out), .sel(SP_PC));
  BusBufferCntrl busbuffercntrl_1 (.A_Out(DOUT), .A_In(B_dout), .Control(or_1_out));
  or or_1 (or_1_out, demultiplexer_2_out1, demultiplexer_2_out2, demultiplexer_2_out3, demultiplexer_2_out4, demultiplexer_2_out5, demultiplexer_2_out6);
  Multiplexer #(.width(16)) multiplexer_3 (.in0(16'h1), .in1({16{1'b1}}), .out(multiplexer_3_out), .sel(INC_DEC));
  Demultiplexer #(.enable("true"), .select(3)) demultiplexer_2 (
    .out0(A_OE), .out1(demultiplexer_2_out1), .out2(demultiplexer_2_out2), .out3(demultiplexer_2_out3),
    .out4(demultiplexer_2_out4), .out5(demultiplexer_2_out5), .out6(demultiplexer_2_out6), .in(OE),
    .sel(DataMUL), .en(OE));  // open: out7
  Adder #(.width(16)) adder_1 (
    .a(multiplexer_2_out), .b(multiplexer_3_out), .out(adder_1_out), .cin(1'b0));  // open: cout
endmodule

module regs16 (
  input  OE,
  input  SELECTHL,
  input  [7:0] DIN,
  input  WE,
  input  R,
  input  CLK,
  output [7:0] DOUT,
  output [15:0] D_Out
);

  wire and_1_out, and_2_out, and_3_out, and_4_out;

  and and_1 (and_1_out, OE, SELECTHL);
  and and_2 (and_2_out, ~SELECTHL, OE);  // AND_Gate
  and and_3 (and_3_out, WE, SELECTHL);
  and and_4 (and_4_out, ~SELECTHL, WE);  // AND_Gate
  Register SPH (.D(DIN), .en(and_3_out), .clk(CLK), .Q(D_Out[15:8]), .clr(R));
  Register SPL (.D(DIN), .en(and_4_out), .clk(CLK), .Q(D_Out[7:0]), .clr(R));
  BusBufferCntrl busbuffercntrl_1 (.A_Out(DOUT), .A_In(D_Out[15:8]), .Control(and_1_out));
  BusBufferCntrl busbuffercntrl_2 (.A_Out(DOUT), .A_In(D_Out[7:0]), .Control(and_2_out));
endmodule

module stack_pointer (
  input  WE,
  input  [15:0] DIN,
  input  R,
  input  CLK,
  output [15:0] D_Out
);

  Register SPH (.D(DIN[15:8]), .en(WE), .clk(CLK), .Q(D_Out[15:8]), .clr(R));
  Register SPL (.D(DIN[7:0]), .en(WE), .clk(CLK), .Q(D_Out[7:0]), .clr(R));
endmodule

module HL (
  input  OE_H,
  input  [7:0] DIN_H,
  input  WE_H,
  input  WE_L,
  input  OE_L,
  input  R,
  input  [7:0] DIN_L,
  input  CLK,
  output [7:0] DOUT_H,
  output [15:0] D_Out,
  output [7:0] DOUT_L
);

  Register H (.D(DIN_H), .en(WE_H), .clk(CLK), .Q(D_Out[15:8]), .clr(R));
  Register L (.D(DIN_L), .en(WE_L), .clk(CLK), .Q(D_Out[7:0]), .clr(R));
  BusBufferCntrl busbuffercntrl_1 (.A_Out(DOUT_H), .A_In(D_Out[15:8]), .Control(OE_H));
  BusBufferCntrl busbuffercntrl_2 (.A_Out(DOUT_L), .A_In(D_Out[7:0]), .Control(OE_L));
endmodule

module PC (
  input  [15:0] DIN,
  input  WE,
  input  R,
  input  CLK,
  output [15:0] D_Out
);

  Register #(.trigger("falling")) PCH (.D(DIN[15:8]), .en(WE), .clk(CLK), .Q(D_Out[15:8]), .clr(R));
  Register #(.trigger("falling")) PCL (.D(DIN[7:0]), .en(WE), .clk(CLK), .Q(D_Out[7:0]), .clr(R));
endmodule

module AddrBufCntrl (
  input  Control,
  input  [15:0] A_In,
  output [15:0] A_Out
);

  assign A_Out[15] = Control ? A_In[8] : 1'bz;  // Controlled_Buffer controlled_buffer_1
  assign A_Out[0] = Control ? A_In[0] : 1'bz;  // Controlled_Buffer controlled_buffer_2
  assign A_Out[14] = Control ? A_In[9] : 1'bz;  // Controlled_Buffer controlled_buffer_3
  assign A_Out[1] = Control ? A_In[1] : 1'bz;  // Controlled_Buffer controlled_buffer_4
  assign A_Out[13] = Control ? A_In[10] : 1'bz;  // Controlled_Buffer controlled_buffer_5
  assign A_Out[2] = Control ? A_In[2] : 1'bz;  // Controlled_Buffer controlled_buffer_6
  assign A_Out[12] = Control ? A_In[11] : 1'bz;  // Controlled_Buffer controlled_buffer_7
  assign A_Out[3] = Control ? A_In[3] : 1'bz;  // Controlled_Buffer controlled_buffer_8
  assign A_Out[11] = Control ? A_In[12] : 1'bz;  // Controlled_Buffer controlled_buffer_9
  assign A_Out[4] = Control ? A_In[4] : 1'bz;  // Controlled_Buffer controlled_buffer_10
  assign A_Out[10] = Control ? A_In[13] : 1'bz;  // Controlled_Buffer controlled_buffer_11
  assign A_Out[5] = Control ? A_In[5] : 1'bz;  // Controlled_Buffer controlled_buffer_12
  assign A_Out[9] = Control ? A_In[14] : 1'bz;  // Controlled_Buffer controlled_buffer_13
  assign A_Out[6] = Control ? A_In[6] : 1'bz;  // Controlled_Buffer controlled_buffer_14
  assign A_Out[8] = Control ? A_In[15] : 1'bz;  // Controlled_Buffer controlled_buffer_15
  assign A_Out[7] = Control ? A_In[7] : 1'bz;  // Controlled_Buffer controlled_buffer_16
endmodule

module count (
  input  CLK,
  input  RST,
  output [1:0] CNT
);

  wire and_1_out, j_k_ff_1_qn, or_1_out;

  or or_1 (or_1_out, RST, and_1_out);
  J_K_Flip_Flop j_k_ff_1 (
    .J(1'b1), .K(1'b1), .clk(CLK), .Q(CNT[0]), .Qn(j_k_ff_1_qn), .reset(or_1_out));  // open: preset
  J_K_Flip_Flop j_k_ff_2 (.J(1'b1), .K(1'b1), .clk(j_k_ff_1_qn), .Q(CNT[1]), .reset(or_1_out));  // open: Qn, preset
  and and_1 (and_1_out, CNT[0], CNT[1]);
endmodule

module control (
  input  C2,
  input  [1:0] EXC,
  input  MOV,
  input  MEM_MOV,
  input  MEM_DIR,
  input  SP_OP,
  input  PUSH,
  input  MIV,
  input  LSP,
  input  LPC,
  input  JS,
  input  [3:0] FLAGS,
  input  [1:0] FMUX,
  input  JR,
  input  CMP,
  input  ALUOP,
  input  [2:0] REGMUX_I,
  output PC_WE,
  output SP_PC,
  output [1:0] ADDR_MUX,
  output IR_WE,
  output R_MUX_CTRL,
  output R_WE,
  output TMP_OE,
  output TMP_WE,
  output R_OE,
  output MEM_W,
  output HL_OE,
  output MEM_R,
  output INC_DEC,
  output SP_WE,
  output ALU_OE,
  output [2:0] REGMUX_O
);

  wire and_1_out, and_3_out, and_4_out, and_5_out, and_6_out, and_7_out, and_8_out, and_9_out, and_10_out,
       and_11_out, and_12_out, and_13_out, and_14_out, and_15_out, and_18_out, and_19_out, and_20_out,
       and_21_out, and_23_out, and_24_out, and_25_out, and_26_out, and_27_out, and_28_out, and_31_out,
       bitselector_1_out, not_1_out, not_2_out, not_3_out, not_4_out, not_5_out, or_1_out, or_2_out,
       or_3_out, or_4_out, or_6_out;
  wire [2:2] not_6_out;

  BitSelector #(.width(4)) bitselector_1 (.in(FLAGS), .out(bitselector_1_out), .sel(FMUX));
  and and_1 (and_1_out, ~C2, and_3_out);  // AND_Gate
  and and_2 (IR_WE, C2, and_3_out);
  and and_3 (and_3_out, ~EXC[0], ~EXC[1]);  // AND_Gate
  and and_4 (and_4_out, EXC[0], ~EXC[1]);  // AND_Gate
  and and_5 (and_5_out, ~EXC[0], EXC[1]);  // AND_Gate
  not not_1 (not_1_out, C2);
  not not_2 (not_2_out, not_1_out);
  or or_1 (or_1_out, and_26_out, IR_WE);
  and and_6 (and_6_out, MOV, ~MEM_MOV);  // AND_Gate
  and and_7 (and_7_out, MOV, MEM_MOV);
  and and_8 (and_8_out, SP_OP, not_2_out, PUSH);
  and and_9 (and_9_out, SP_OP, not_2_out, ~PUSH);  // AND_Gate
  and and_10 (and_10_out, and_4_out, MIV);
  and and_11 (and_11_out, not_2_out, and_5_out, LSP);
  and and_12 (and_12_out, ~not_2_out, and_4_out, LPC);  // AND_Gate
  and and_13 (and_13_out, and_4_out, ~not_2_out, bitselector_1_out, JS);  // AND_Gate
  and and_14 (and_14_out, and_4_out, ~not_2_out, ~bitselector_1_out, JR);  // AND_Gate
  and and_15 (and_15_out, not_2_out, and_4_out, ALUOP);
  and and_16 (ALU_OE, ALUOP, and_5_out, not_2_out);
  not not_3 (not_3_out, or_1_out);
  not not_4 (not_4_out, or_2_out);
  and and_17 (TMP_OE, and_5_out, and_6_out);
  and and_18 (and_18_out, and_4_out, and_6_out);
  and and_19 (and_19_out, and_7_out, and_4_out, MEM_DIR, not_2_out);
  and and_20 (and_20_out, and_7_out, ~MEM_DIR, and_5_out, not_2_out);  // AND_Gate
  or or_2 (or_2_out, and_21_out, and_24_out);
  and and_21 (and_21_out, and_4_out, and_8_out);
  and and_22 (INC_DEC, and_5_out, and_8_out);
  and and_23 (and_23_out, and_4_out, and_9_out);
  and and_24 (and_24_out, and_9_out, and_5_out);
  and and_25 (and_25_out, ~not_2_out, and_10_out);  // AND_Gate
  and and_26 (and_26_out, not_2_out, and_10_out);
  or or_3 (or_3_out, and_12_out, and_13_out, and_14_out);
  not not_5 (not_5_out, ALU_OE);
  assign REGMUX_O = not_5_out ? REGMUX_I : 3'bz;  // Controlled_Buffer controlled_buffer_1
  and and_27 (and_27_out, not_3_out, not_4_out);
  and and_28 (and_28_out, not_3_out, and_7_out);
  and and_29 (ADDR_MUX[0], not_3_out, ~and_7_out);  // AND_Gate
  or or_4 (or_4_out, INC_DEC, and_23_out);
  not not_6 (not_6_out[2], ALU_OE);
  assign REGMUX_O = ALU_OE ? {3{not_6_out[2]}} : 3'bz;  // Controlled_Buffer controlled_buffer_2
  or or_5 (ADDR_MUX[1], and_27_out, and_28_out);
  or or_6 (or_6_out, and_1_out, and_25_out);
  and and_30 (SP_PC, or_6_out, ~and_11_out);  // AND_Gate
  and and_31 (and_31_out, ALU_OE, ~CMP);  // AND_Gate
  or or_7 (PC_WE, or_3_out, SP_PC);
  or or_8 (R_MUX_CTRL, TMP_OE, and_24_out, and_20_out);
  or or_9 (R_WE, TMP_OE, and_20_out, and_31_out, and_26_out, and_24_out);
  or or_10 (TMP_WE, and_15_out, and_18_out);
  or or_11 (R_OE, and_15_out, and_18_out, and_19_out, and_21_out);
  or or_12 (MEM_W, and_19_out, and_21_out);
  or or_13 (HL_OE, and_19_out, and_20_out, and_11_out, or_3_out);
  or or_14 (MEM_R, and_20_out, and_26_out, IR_WE, and_24_out);
  or or_15 (SP_WE, or_4_out, and_11_out);

  // Notes on the sheet:
  //   1
  //   2
endmodule

module InstrReg (
  input  WE,
  input  R,
  input  [7:0] DIN,
  input  CLK,
  output [7:0] D_Out
);

  Register register_1 (.D(DIN), .en(WE), .clk(CLK), .Q(D_Out), .clr(R));
endmodule

module keybord (
);

  wire button_1_out, clock_1_out, demultiplexer_1_out0, demultiplexer_1_out1, demultiplexer_1_out2,
       demultiplexer_1_out3, pull_resistor_1_node, pull_resistor_2_node, pull_resistor_3_node,
       pull_resistor_4_node, pull_resistor_5_node, pull_resistor_6_node, pull_resistor_7_node,
       pull_resistor_8_node, pull_resistor_9_node, pull_resistor_10_node;
  wire [1:0] not_1_out;

  Clock clock_1 (.out(clock_1_out));
  Button button_1 (.out(button_1_out));
  J_K_Flip_Flop j_k_ff_1 (.J(1'b1), .K(1'b1), .clk(clock_1_out), .Q(not_1_out[1]));  // open: Qn, preset, reset
  not not_1 (not_1_out[0], clock_1_out);
  Demultiplexer #(.select(2)) demultiplexer_1 (
    .out0(demultiplexer_1_out0), .out1(demultiplexer_1_out1), .out2(demultiplexer_1_out2),
    .out3(demultiplexer_1_out3), .in(1'b1), .sel(not_1_out));
  Pull_Resistor pull_resistor_1 (.node(pull_resistor_1_node));
  Pull_Resistor pull_resistor_2 (.node(pull_resistor_2_node));
  // Switch n1: pin names not known; wires that end beside it: demultiplexer_1_out0, pull_resistor_1_node
  // Switch n2: pin names not known; wires that end beside it: demultiplexer_1_out0, pull_resistor_2_node
  // Switch q: pin names not known; wires that end beside it: 1'b1, demultiplexer_1_out1, pull_resistor_1_node
  // Switch w: pin names not known; wires that end beside it: demultiplexer_1_out1, pull_resistor_2_node
  // Switch a: pin names not known; wires that end beside it: demultiplexer_1_out2, pull_resistor_1_node
  // Switch s: pin names not known; wires that end beside it: demultiplexer_1_out2, pull_resistor_2_node
  // Switch z: pin names not known; wires that end beside it: demultiplexer_1_out3, pull_resistor_1_node
  // Switch x: pin names not known; wires that end beside it: demultiplexer_1_out3, pull_resistor_2_node
  Pull_Resistor pull_resistor_3 (.node(pull_resistor_3_node));
  // Switch n3: pin names not known; wires that end beside it: demultiplexer_1_out0, pull_resistor_3_node
  // Switch e: pin names not known; wires that end beside it: demultiplexer_1_out1, pull_resistor_3_node
  // Switch d: pin names not known; wires that end beside it: demultiplexer_1_out2, pull_resistor_3_node
  // Switch c: pin names not known; wires that end beside it: demultiplexer_1_out3, pull_resistor_3_node
  Pull_Resistor pull_resistor_4 (.node(pull_resistor_4_node));
  // Switch n4: pin names not known; wires that end beside it: demultiplexer_1_out0, pull_resistor_4_node
  // Switch r: pin names not known; wires that end beside it: demultiplexer_1_out1, pull_resistor_4_node
  // Switch f: pin names not known; wires that end beside it: demultiplexer_1_out2, pull_resistor_4_node
  // Switch v: pin names not known; wires that end beside it: demultiplexer_1_out3, pull_resistor_4_node
  Pull_Resistor pull_resistor_5 (.node(pull_resistor_5_node));
  Pull_Resistor pull_resistor_6 (.node(pull_resistor_6_node));
  // Switch n5: pin names not known; wires that end beside it: demultiplexer_1_out0, pull_resistor_5_node
  // Switch n6: pin names not known; wires that end beside it: demultiplexer_1_out0, pull_resistor_6_node
  // Switch t: pin names not known; wires that end beside it: demultiplexer_1_out1, pull_resistor_5_node
  // Switch y: pin names not known; wires that end beside it: demultiplexer_1_out1, pull_resistor_6_node
  // Switch g: pin names not known; wires that end beside it: demultiplexer_1_out2, pull_resistor_5_node
  // Switch h: pin names not known; wires that end beside it: demultiplexer_1_out2, pull_resistor_6_node
  // Switch b: pin names not known; wires that end beside it: demultiplexer_1_out3, pull_resistor_5_node
  // Switch n: pin names not known; wires that end beside it: demultiplexer_1_out3, pull_resistor_6_node
  Pull_Resistor pull_resistor_7 (.node(pull_resistor_7_node));
  // Switch n7: pin names not known; wires that end beside it: demultiplexer_1_out0, pull_resistor_7_node
  // Switch u: pin names not known; wires that end beside it: demultiplexer_1_out1, pull_resistor_7_node
  // Switch j: pin names not known; wires that end beside it: demultiplexer_1_out2, pull_resistor_7_node
  // Switch m: pin names not known; wires that end beside it: demultiplexer_1_out3, pull_resistor_7_node
  Pull_Resistor pull_resistor_8 (.node(pull_resistor_8_node));
  // Switch n8: pin names not known; wires that end beside it: demultiplexer_1_out0, pull_resistor_8_node
  // Switch i: pin names not known; wires that end beside it: demultiplexer_1_out1, pull_resistor_8_node
  // Switch k: pin names not known; wires that end beside it: demultiplexer_1_out2, pull_resistor_8_node
  // Switch space: pin names not known; wires that end beside it: demultiplexer_1_out3, pull_resistor_8_node
  Pull_Resistor pull_resistor_9 (.node(pull_resistor_9_node));
  Pull_Resistor pull_resistor_10 (.node(pull_resistor_10_node));
  // Switch n9: pin names not known; wires that end beside it: demultiplexer_1_out0, pull_resistor_9_node
  // Switch n0: pin names not known; wires that end beside it: demultiplexer_1_out0, pull_resistor_10_node
  // Switch o: pin names not known; wires that end beside it: demultiplexer_1_out1, pull_resistor_9_node
  // Switch p: pin names not known; wires that end beside it: demultiplexer_1_out1, pull_resistor_10_node
  // Switch l: pin names not known; wires that end beside it: demultiplexer_1_out2, pull_resistor_9_node
  // Switch Enter: pin names not known; wires that end beside it: demultiplexer_1_out2, pull_resistor_10_node
  // Switch shift: pin names not known; wires that end beside it: demultiplexer_1_out3, pull_resistor_9_node
  // Switch backspace: pin names not known; wires that end beside it: demultiplexer_1_out3, pull_resistor_10_node
endmodule

module addrdec (
  input  [15:0] Address,
  input  MR,
  input  MW,
  output [14:0] addr,
  output ROM_E,
  output RAM_R,
  output RAM_W,
  output KEY_CTRL,
  output KEY_DATA,
  output X_POS,
  output Y_POS,
  output SCR_DATA
);

  wire and_2_out, and_3_out, and_4_out, and_5_out, and_13_out;

  and and_1 (ROM_E, ~Address[15], MR, ~MW);  // AND_Gate
  and and_2 (and_2_out, Address[15], MR, ~MW);  // AND_Gate
  and and_3 (and_3_out, Address[15], ~MR, MW);  // AND_Gate
  and and_4 (and_4_out, Address[12], Address[13], Address[14], Address[15]);
  and and_5 (and_5_out, ~Address[4], ~Address[5], ~Address[6], ~Address[7], ~Address[8], ~Address[9], ~Address[10], ~Address[11]);  // AND_Gate
  and and_6 (KEY_CTRL, ~Address[0], ~Address[1], and_13_out, ~Address[2], ~Address[3], MW);  // AND_Gate
  and and_7 (KEY_DATA, Address[0], ~Address[1], and_13_out, ~Address[2], ~Address[3], MR);  // AND_Gate
  and and_8 (X_POS, ~Address[0], Address[1], and_13_out, ~Address[2], ~Address[3], MW);  // AND_Gate
  and and_9 (Y_POS, Address[0], Address[1], and_13_out, ~Address[2], ~Address[3], MW);  // AND_Gate
  and and_10 (SCR_DATA, ~Address[0], ~Address[1], and_13_out, Address[2], ~Address[3], MW);  // AND_Gate
  and and_11 (RAM_R, and_2_out, ~and_4_out);  // AND_Gate
  and and_12 (RAM_W, and_3_out, ~and_4_out);  // AND_Gate
  and and_13 (and_13_out, and_4_out, and_5_out);

  assign addr = Address[14:0];
endmodule
